# Fritzing sketch circuit (saved by Fritzing 0.7.12b)
breadboards: 2

parts:
  Arduino_Ethernet_Shield1 = Arduino Ethernet Shield
  R1 = Resistor [tolerance=±5% resistance=10k package=THT]

nets:
  N1: Arduino_Ethernet_Shield1.D3, R1.Pin_0
  N2: Arduino_Ethernet_Shield1.A2, R1.Pin_1
